# Fritzing sketch setup so far (saved by Fritzing 0.9.0b)
breadboards: 1

parts:
  Part1 = Arduino Uno (Rev3)
  R1 = Resistor [package="0402 [SMD]"]
  LED1 = LED - 5mm [color="Yellow (595nm)" package="5 mm [THT]"]
  R2 = Resistor [package="0402 [SMD]"]
  R3 = Resistor [package="0402 [SMD]"]
  R4 = Resistor [package="0402 [SMD]"]
  LED2 = LED - 5mm [color="Yellow (595nm)" package="5 mm [THT]"]
  LED3 = LED - 5mm [color="Yellow (595nm)" package="5 mm [THT]"]
  LED4 = LED - 5mm [color="Yellow (595nm)" package="5 mm [THT]"]
  LED5 = RGB LED (com. cathode, rgb) [package="5 mm [THT]"]
  R5 = Resistor [tolerance=±5% resistance=330k package=THT]
  R6 = Resistor [tolerance=±5% resistance=330k package=THT]
  R7 = Resistor [tolerance=±5% resistance=330k package=THT]

nets:
  N1: Part1.D8, LED2.cathode
  N2: Part1.D9_PWM, LED3.cathode
  N3: Part1.D10_PWM/SS, LED4.cathode
  N4: Part1.D11_PWM/MOSI, LED5.red_anode, R5.Pin_0, R5.Pin_1
  N5: Part1.D12/MISO, LED5.green_anode, R7.Pin_0, R7.Pin_1
  N6: Part1.D13/SCK, LED5.blue_anode, R6.Pin_0, R6.Pin_1
  N7: Part1.D7, LED1.cathode
  N8: Part1.GND, R1.Pin_0, R2.Pin_0, R3.Pin_0, R4.Pin_0, LED5.common_cathode
  N9: R1.Pin_1, LED1.anode
  N10: R2.Pin_1, LED2.anode
  N11: R3.Pin_1, LED3.anode
  N12: R4.Pin_1, LED4.anode
